// Logisim project SCHEMATIC.circ as structural Verilog
module PC (
  input  [7:0] INPUT,
  input  SEL,
  input  CLK,
  input  RST,
  input  [7:0] OUTPUT
);

  wire [7:0] multiplexer_1_out, reg_8bit_1_output;

  REG_8BIT reg_8bit_1 (.INPUT(OUTPUT), .CLK(CLK), .RST(RST), .OUTPUT(reg_8bit_1_output));
  Multiplexer #(.width(8), .enable("false")) multiplexer_1 (
    .in0(8'h1), .in1(INPUT), .out(multiplexer_1_out), .sel(SEL));
  Adder adder_1 (.a(multiplexer_1_out), .b(reg_8bit_1_output), .out(OUTPUT));  // open: cin, cout
endmodule

module REGISTER (
  input  [15:0] INPUT,
  input  CLK,
  input  RST,
  output [15:0] OUTPUT
);

  Register #(.width(16)) register_1 (.D(INPUT), .en(1'b1), .Q(OUTPUT), .clk(CLK), .clr(RST));
endmodule

module ALU (
  input  CLK,
  input  [15:0] IN_A,
  input  [15:0] IN_B,
  input  ENABLE,
  input  [4:0] OPCODE,
  output [15:0] OUTPUT
);

  wire [3:0] bitselector_1_out, undriven;
  wire [15:0] adder_1_out, and_1_out, negator_1_out, or_1_out, subtractor_1_out, xor_1_out;

  Adder #(.width(16)) adder_1 (.a(IN_A), .b(IN_B), .out(adder_1_out));  // open: cin, cout
  Subtractor #(.width(16)) subtractor_1 (.a(IN_A), .b(IN_B), .out(subtractor_1_out));  // open: bin, bout
  assign and_1_out = IN_A & IN_B;  // AND_Gate and_1, 16 bits wide
  assign or_1_out = IN_A | IN_B;  // OR_Gate or_1, 16 bits wide
  assign xor_1_out = IN_A ^ IN_B;  // XOR_Gate xor_1, 16 bits wide
  Negator #(.width(16)) negator_1 (.in(IN_A), .out(negator_1_out));
  Comparator #(.width(4)) comparator_1 (.b(bitselector_1_out));  // open: a, gt, eq, lt
  Comparator #(.width(4)) comparator_2 (.a(undriven), .b(bitselector_1_out));  // open: gt, eq, lt
  Multiplexer #(.select(4), .width(16)) multiplexer_1 (
    .in1(adder_1_out), .in2(adder_1_out), .in3(subtractor_1_out), .in4(subtractor_1_out), .in5(and_1_out),
    .in6(or_1_out), .in7(xor_1_out), .in8(negator_1_out), .out(OUTPUT), .sel(bitselector_1_out), .en(ENABLE));  // open: in0, in9, in10, in11, in12, in13, in14, in15
  BitSelector #(.width(5), .group(4)) bitselector_1 (.in(OPCODE), .out(bitselector_1_out), .sel(1'b0));
endmodule

module RAM (
  input  READ,
  input  in_2,
  input  CLK,
  input  RST,
  input  WRITE,
  output out_6
);

  RAM_part #(.dataWidth(16), .bus("separate")) ram_1 (
    .clk(CLK), .ld(WRITE), .clr(RST));  // open: addr, din, data, str, sel
endmodule

module CPU_REGISTERS (
  input  [15:0] IN,
  input  CLK,
  input  RST,
  input  [2:0] SEL_OUT,
  input  [2:0] SEL_OUT2,
  input  [2:0] SEL_IN,
  input  OUTPUT_EN,
  input  WRITE_EN,
  output [15:0] OUT,
  output [15:0] OUT2
);

  wire undriven, undriven_2;
  wire [15:0] demultiplexer_1_out0, demultiplexer_1_out1, demultiplexer_1_out2, demultiplexer_1_out3,
       demultiplexer_1_out4, demultiplexer_1_out5, demultiplexer_1_out6, demultiplexer_1_out7, register_1_q,
       register_2_q, register_3_q, register_4_q, register_5_q, register_6_q, register_7_q, register_8_q;

  Register #(.width(16)) register_1 (
    .D(demultiplexer_1_out0), .en(1'b1), .Q(register_1_q), .clk(undriven_2), .clr(undriven));
  Multiplexer #(.select(3), .width(16)) multiplexer_1 (
    .in0(register_1_q), .in1(register_2_q), .in2(register_3_q), .in3(register_4_q), .in4(register_5_q),
    .in5(register_7_q), .in6(register_6_q), .in7(register_8_q), .out(OUT), .sel(SEL_OUT), .en(OUTPUT_EN));
  Register #(.width(16)) register_2 (
    .D(demultiplexer_1_out1), .en(1'b1), .Q(register_2_q), .clk(undriven_2), .clr(undriven));
  Register #(.width(16)) register_3 (
    .D(demultiplexer_1_out2), .en(1'b1), .Q(register_3_q), .clk(undriven_2), .clr(undriven));
  Register #(.width(16)) register_4 (
    .D(demultiplexer_1_out3), .en(1'b1), .Q(register_4_q), .clk(undriven_2), .clr(undriven));
  Register #(.width(16)) register_5 (
    .D(demultiplexer_1_out4), .en(1'b1), .Q(register_5_q), .clk(undriven_2), .clr(undriven));
  Multiplexer #(.select(3), .width(16)) multiplexer_2 (
    .in0(register_1_q), .in1(register_2_q), .in2(register_3_q), .in3(register_4_q), .in4(register_5_q),
    .in5(register_7_q), .in6(register_6_q), .in7(register_8_q), .out(OUT2), .sel(SEL_OUT2), .en(OUTPUT_EN));
  Register #(.width(16)) register_6 (
    .D(demultiplexer_1_out6), .en(1'b1), .Q(register_6_q), .clk(undriven_2), .clr(undriven));
  Register #(.width(16)) register_7 (
    .D(demultiplexer_1_out5), .en(1'b1), .Q(register_7_q), .clk(undriven_2), .clr(undriven));
  Register #(.width(16)) register_8 (
    .D(demultiplexer_1_out7), .en(1'b1), .Q(register_8_q), .clk(undriven_2), .clr(undriven));
  Demultiplexer #(.select(3), .width(16)) demultiplexer_1 (
    .out0(demultiplexer_1_out0), .out1(demultiplexer_1_out1), .out2(demultiplexer_1_out2),
    .out3(demultiplexer_1_out3), .out4(demultiplexer_1_out4), .out5(demultiplexer_1_out5),
    .out6(demultiplexer_1_out6), .out7(demultiplexer_1_out7), .in(IN), .sel(SEL_IN), .en(WRITE_EN));
endmodule

module REG_8BIT (
  input  [7:0] INPUT,
  input  CLK,
  input  RST,
  output [7:0] OUTPUT
);

  Register register_1 (.D(INPUT), .en(1'b1), .Q(OUTPUT), .clk(CLK), .clr(RST));
endmodule
